// Logisim project TP3_AC2_Vinicius_Henrique_Giovanini.circ as structural Verilog: 5 circuits, main circuit meiasoma
module meiasoma (
  input  a0,
  input  b0,
  output s0,
  output co0
);

  and and_1 (co0, b0, a0);
  xor xor_1 (s0, a0, b0);
endmodule

module soma_1bit (
  input  CIN,
  input  A0,
  input  B0,
  output SO0,
  output CO0
);

  wire meiasoma_1_co0, meiasoma_1_s0, meiasoma_2_co0;

  meiasoma meiasoma_1 (.a0(A0), .b0(B0), .co0(meiasoma_1_co0), .s0(meiasoma_1_s0));
  or or_1 (CO0, meiasoma_1_co0, meiasoma_2_co0);
  meiasoma meiasoma_2 (.a0(CIN), .b0(meiasoma_1_s0), .co0(meiasoma_2_co0), .s0(SO0));
endmodule

// ULA1B
module ULA_1_BIT (
  input  CIN,
  input  A,
  input  [1:0] Seletor_Mux_4x1,
  input  B,
  input  Binvert,
  output \Saída ,
  output Cout
);

  wire and_1_out, multiplexer_1_out, not_1_out, not_2_out, or_1_out, soma_1bit_1_so0;

  not not_1 (not_1_out, B);
  Multiplexer #(.enable("false")) multiplexer_1 (.in0(B), .in1(not_1_out), .out(multiplexer_1_out), .sel(Binvert));
  and and_1 (and_1_out, A, multiplexer_1_out);
  or or_1 (or_1_out, A, multiplexer_1_out);
  not not_2 (not_2_out, A);
  soma_1bit soma_1bit_1 (.A0(A), .B0(multiplexer_1_out), .CIN(CIN), .CO0(Cout), .SO0(soma_1bit_1_so0));
  Multiplexer #(.select(2), .enable("false")) multiplexer_2 (
    .in0(and_1_out), .in1(or_1_out), .in2(not_2_out), .in3(soma_1bit_1_so0), .out(\Saída ),
    .sel(Seletor_Mux_4x1));
endmodule

module ULA_2_BIT (
  input  Binvert,
  input  [1:0] in_2,
  input  CIN,
  input  A0,
  input  B0,
  input  A1,
  input  B1,
  output S0,
  output S1,
  output COUT
);

  wire ula_1_bit_1_cout;

  ULA_1_BIT ula_1_bit_1 (
    .A(A0), .B(B0), .CIN(CIN), .Binvert(Binvert), .Cout(ula_1_bit_1_cout), .Seletor_Mux_4x1(in_2),
    .\Saída (S0));
  ULA_1_BIT ula_1_bit_2 (
    .A(A1), .B(B1), .CIN(ula_1_bit_1_cout), .Binvert(Binvert), .Cout(COUT), .Seletor_Mux_4x1(in_2),
    .\Saída (S1));
endmodule

module ULA_4_BIT (
  input  [1:0] SELETOR,
  input  Binvert,
  input  CIN,
  input  A0,
  input  B0,
  input  A1,
  input  B1,
  input  A2,
  input  B2,
  input  A3,
  input  B3,
  output S0,
  output S1,
  output S2,
  output S3,
  output COUT
);

  wire ula_2_bit_1_cout;

  ULA_2_BIT ula_2_bit_1 (
    .A0(A0), .B0(B0), .A1(A1), .B1(B1), .Binvert(Binvert), .CIN(CIN), .in_2(SELETOR),
    .COUT(ula_2_bit_1_cout), .S0(S0), .S1(S1));
  ULA_2_BIT ula_2_bit_2 (
    .A0(A2), .B0(B2), .A1(A3), .B1(B3), .Binvert(Binvert), .CIN(ula_2_bit_1_cout), .in_2(SELETOR),
    .COUT(COUT), .S0(S2), .S1(S3));
endmodule
